# Fritzing sketch aqm mk II (saved by Fritzing 0.9.3b)
breadboards: 1

parts:
  J1 = female pin header, 7 pins [form="♀ (female)"]
  J2 = female pin header, 7 pins [form="♀ (female)"]
  Part4 = Adafruit BME680
  MCU1 = Raspberry Pi 3 [part_number=RPI-3-V1.2]
  U2 = mystery part, 8 pins [chip_label=PMS5003]

nets:
  N1: J1.pin3, J2.pin2
  GND: Part4.GND, MCU1.GND, U2.pin2
  N2: MCU1.GPIO18, U2.pin5
  N3: MCU1.5V, U2.pin1

notes:
  BME680
  temperature, humidity, barometric pressure, and VOC gas
  PMS5003
  PM1.0, PM2.5 and PM10.0 concentration in both standard & enviromental units
  Particulate matter per 0.1L air, categorized into 0.3um, 0.5um, 1.0um, 2.5um, 5.0um and 10um size bins
